// Logisim project ALU.circ as structural Verilog: 1 circuit, main circuit main
module main (
  input  A0,
  input  A1,
  input  A2,
  input  A3,
  input  A4,
  input  A5,
  input  A6,
  input  A7,
  input  B0,
  input  B1,
  input  B2,
  input  B3,
  input  B4,
  input  B5,
  input  B6,
  input  B7,
  input  OP_CODE_0,
  input  OP_CODE_1,
  input  OP_CODE_2,
  output [7:0] out_20,
  output [3:0] NZCV
);

  wire adder_1_cout, adder_2_cout, addition_Overflow_out, Left_Shift_carry, not_2_out, not_3_out, not_4_out,
       not_5_out, O_P_1_prime_2_out, O_P_2_prime_1_prime_out, O_P_prime_1_2_out, O_P_prime_2_prime_1_out,
       or_2_out, Shift_Right_carry, Subtraction_Overflow_out;
  wire [7:0] adder_1_out, adder_2_out, and_1_out, Left_Shift_new_bits_shift_to_left, not_1_out, or_1_out,
       Shift_Right_new_bits_shift_to_right, xor_1_out;

  assign not_1_out = ~{B7, B6, B5, B4, B3, B2, B1, B0};  // NOT_Gate not_1, 8 bits wide
  Adder adder_1 (
    .a({A7, A6, A5, A4, A3, A2, A1, A0}), .b({B7, B6, B5, B4, B3, B2, B1, B0}), .out(adder_1_out),
    .cout(adder_1_cout));  // open: cin
  Adder adder_2 (
    .a({A7, A6, A5, A4, A3, A2, A1, A0}), .b(not_1_out), .out(adder_2_out), .cin(1'b1), .cout(adder_2_cout));
  assign and_1_out = {A7, A6, A5, A4, A3, A2, A1, A0} & {B7, B6, B5, B4, B3, B2, B1, B0};  // AND_Gate and_1, 8 bits wide
  assign or_1_out = {A7, A6, A5, A4, A3, A2, A1, A0} | {B7, B6, B5, B4, B3, B2, B1, B0};  // OR_Gate or_1, 8 bits wide
  assign xor_1_out = {A7, A6, A5, A4, A3, A2, A1, A0} ^ {B7, B6, B5, B4, B3, B2, B1, B0};  // XOR_Gate xor_1, 8 bits wide
  Shifter_to_left_main Left_Shift (
    .Old_Bits({A7, A6, A5, A4, A3, A2, A1, A0}), .New_Bits_shift_to_left(Left_Shift_new_bits_shift_to_left),
    .Carry(Left_Shift_carry));
  Shifter_to_rightt_main Shift_Right (
    .Old_Bits({A7, A6, A5, A4, A3, A2, A1, A0}), .Carry(Shift_Right_carry),
    .New_Bits_shift_to_right(Shift_Right_new_bits_shift_to_right));
  not not_2 (not_2_out, A7);
  not not_3 (not_3_out, B7);
  not not_4 (not_4_out, adder_2_out[7]);
  not not_5 (not_5_out, adder_1_out[7]);
  and O_P_prime_2_prime_1 (O_P_prime_2_prime_1_out, not_4_out, A7, not_3_out);
  and O_P_1_prime_2 (O_P_1_prime_2_out, adder_2_out[7], not_2_out, B7);
  and O_P_2_prime_1_prime (O_P_2_prime_1_prime_out, not_2_out, not_3_out, adder_1_out[7]);
  and O_P_prime_1_2 (O_P_prime_1_2_out, not_5_out, A7, B7);
  or Subtraction_Overflow (Subtraction_Overflow_out, O_P_prime_2_prime_1_out, O_P_1_prime_2_out);
  or addition_Overflow (addition_Overflow_out, O_P_2_prime_1_prime_out, O_P_prime_1_2_out);
  Multiplexer #(.select(3), .width(8), .enable("false")) multiplexer_1 (
    .in0(adder_1_out), .in1(adder_2_out), .in2(and_1_out), .in3(or_1_out), .in4(xor_1_out),
    .in5(Left_Shift_new_bits_shift_to_left), .in6(Shift_Right_new_bits_shift_to_right),
    .in7({A7, A6, A5, A4, A3, A2, A1, A0}), .out({NZCV[3], out_20[6:0]}),
    .sel({OP_CODE_2, OP_CODE_1, OP_CODE_0}));
  Multiplexer #(.select(3), .enable("false")) multiplexer_2 (
    .in0(adder_1_cout), .in1(adder_2_cout), .in2(1'b0), .in3(1'b0), .in4(1'b0), .in5(Left_Shift_carry),
    .in6(Shift_Right_carry), .in7(1'b0), .out(NZCV[1]), .sel({OP_CODE_2, OP_CODE_1, OP_CODE_0}));
  Multiplexer #(.select(3), .enable("false")) multiplexer_3 (
    .in0(addition_Overflow_out), .in1(Subtraction_Overflow_out), .in2(1'b0), .in3(1'b0), .in4(1'b0),
    .in5(1'b0), .in6(1'b0), .in7(1'b0), .out(NZCV[0]), .sel({OP_CODE_2, OP_CODE_1, OP_CODE_0}));
  not not_6 (NZCV[2], or_2_out);
  or or_2 (or_2_out, out_20[0], out_20[1], out_20[2], out_20[3], out_20[4], out_20[5], out_20[6], NZCV[3]);

  assign out_20[7] = NZCV[3];
endmodule
