// Logisim project CPU_Core.circ as structural Verilog: 1 circuit, main circuit main
module main (
  input  Reset,
  output [3:0] NZCV
);

  wire main_1_p3;
  wire [7:0] main_1_p1, main_1_p5;
  wire [23:0] rom_1_data;

  // Program_Counter_main main_1: pin names not known; wires that end beside it: main_1_p1, rom_1_data[10], main_1_p3, Reset, main_1_p5
  ROM #(.dataWidth(24)) rom_1 (.addr(main_1_p5), .data({rom_1_data[23:19], main_1_p1, rom_1_data[10:0]}));  // open: sel
  Clock clock_1 (.out(main_1_p3));
  // _8_bit_Data_path_main main_2: pin names not known; wires that end beside it: rom_1_data[8:7], main_1_p3, rom_1_data[9], rom_1_data[2:0], rom_1_data[4:3], rom_1_data[6:5], NZCV

  // Notes on the sheet:
  //   Bits 0-2 (3 bits): ALU OpCode.  
  //   Bits 3-4 (2 bits): Read Address A.
  //   Bits 5-6 (2 bits): Read Address B.
  //   Bits 7-8 (2 bits): Write Address.
  //   Bit 9 (1 bit): Write Enable.
  //   Bit 10 (1 bit): Jump Enable.
  //   Bit 11 – 18 (8 bits): Jump Address
  //   Bit 19 – 23 (5 bits): Unused
  //   contents of rom_1 (hex, n*v repeats v):
  //   290 3d0 400
endmodule
