// Logisim project Shifter to left.circ as structural Verilog: 1 circuit, main circuit main
module main (
  input  [7:0] Old_Bits,
  output [7:0] New_Bits_shift_to_left,
  output Carry
);


  assign Carry = Old_Bits[7];
  assign New_Bits_shift_to_left = {Old_Bits[6:0], 1'b0};
endmodule
