// Logisim project Shifter to rightt.circ as structural Verilog: 1 circuit, main circuit main
module main (
  input  [7:0] Old_Bits,
  output Carry,
  output [7:0] New_Bits_shift_to_right
);


  assign Carry = Old_Bits[0];
  assign New_Bits_shift_to_right = {1'b0, Old_Bits[7:1]};
endmodule
